# Fritzing sketch potentiometer (saved by Fritzing 0.7.4b)
breadboards: 1

parts:
  Arduino1 = Arduino
  R7 = Rotary Potentiometer (Small) [maximum_resistance=100kΩ]

nets:
  N1: Arduino1.GND, R7.leg1
  N2: Arduino1.+5V, R7.leg2
  N3: Arduino1.A0, R7.wiper
