# Fritzing sketch rgb-led (saved by Fritzing 0.7.4b)
breadboards: 1

parts:
  Arduino = Arduino
  R2 = Resistor [tolerance=±5% resistance=180 package=THT]
  R3 = Resistor [tolerance=±5% resistance=330 package=THT]
  R1 = Resistor [tolerance=±5% resistance=180 package=THT]
  LED1 = RGB LED (com. cathode, rgb) [package="5 mm [THT]"]

nets:
  N1: Arduino.GND, LED1.common_cathode
  N2: Arduino.D6, R2.Pin_0
  N3: Arduino.D5, R1.Pin_0
  N4: Arduino.D3, R3.Pin_0
  N5: R2.Pin_1, LED1.green_anode
  N6: R3.Pin_1, LED1.red_anode
  N7: R1.Pin_1, LED1.blue_anode
